// Logisim project PKA-07.circ as structural Verilog: 9 circuits, main circuit main
module main (
);

  wire button_1_out, button_2_out, button_3_out, button_4_out, button_5_out, button_6_out, button_7_out,
       button_8_out, button_9_out, DAY_jumat, DAY_kamis, DAY_minggu, DAY_rabu, DAY_sabtu, DAY_selasa,
       DAY_senin, lowerdisplay_1_out_2, lowerdisplay_1_out_3, lowerdisplay_1_out_4, lowerdisplay_1_out_5,
       lowerdisplay_1_out_7, lowerdisplay_1_out_8, lowerdisplay_1_out_9, lowerdisplay_1_out_10,
       lowerdisplay_1_out_11, lowerdisplay_1_out_12, lowerdisplay_1_out_14, lowerdisplay_1_out_15,
       lowerdisplay_1_out_16, lowerdisplay_1_out_17, lowerdisplay_1_out_18, lowerdisplay_1_out_19,
       upperdisplay_1_out_8, upperdisplay_1_out_9, upperdisplay_1_out_10, upperdisplay_1_out_11,
       upperdisplay_1_out_12, upperdisplay_1_out_13, upperdisplay_1_out_14, upperdisplay_1_out_15,
       upperdisplay_1_out_16, upperdisplay_1_out_17, upperdisplay_1_out_18, upperdisplay_1_out_19,
       upperdisplay_1_out_21, upperdisplay_1_out_22, upperdisplay_1_out_23, upperdisplay_1_out_24,
       upperdisplay_1_out_25, upperdisplay_1_out_26, upperdisplay_1_out_27, upperdisplay_1_out_28,
       upperdisplay_1_out_29, upperdisplay_1_out_30;
  wire [5:0] lowerdisplay_1_out_6, lowerdisplay_1_out_13, lowerdisplay_1_out_20, lowerdisplay_1_out_21,
       lowerdisplay_1_out_22, lowerdisplay_1_out_23, lowerdisplay_1_out_24, lowerdisplay_1_out_25,
       lowerdisplay_1_out_26;
  wire [16:0] upperdisplay_1_out_20;

  _7_Segment_Display u_7_segment_display_1 (
    .b(upperdisplay_1_out_9), .c(lowerdisplay_1_out_2));  // open: g, f, a, e, d, dp
  Button button_1 (.out(button_1_out));
  _7_Segment_Display u_7_segment_display_2 (
    .g(upperdisplay_1_out_21), .f(upperdisplay_1_out_10), .a(upperdisplay_1_out_22),
    .b(upperdisplay_1_out_11), .e(lowerdisplay_1_out_3), .d(lowerdisplay_1_out_4), .c(lowerdisplay_1_out_5),
    .dp(lowerdisplay_1_out_5));
  DotMatrix #(.matrixcols(1), .matrixrows(6)) dotmatrix_1 (.col0(lowerdisplay_1_out_6));
  Button button_2 (.out(button_2_out));
  Button button_3 (.out(button_3_out));
  Button button_4 (.out(button_4_out));
  Button button_5 (.out(button_5_out));
  _7_Segment_Display u_7_segment_display_3 (
    .g(upperdisplay_1_out_23), .f(upperdisplay_1_out_12), .a(upperdisplay_1_out_24),
    .b(upperdisplay_1_out_13), .e(lowerdisplay_1_out_7), .d(lowerdisplay_1_out_8), .c(lowerdisplay_1_out_9));  // open: dp
  _7_Segment_Display u_7_segment_display_4 (
    .g(upperdisplay_1_out_25), .f(upperdisplay_1_out_14), .a(upperdisplay_1_out_26),
    .b(upperdisplay_1_out_15), .e(lowerdisplay_1_out_10), .d(lowerdisplay_1_out_11), .c(lowerdisplay_1_out_12));  // open: dp
  Button button_6 (.out(button_6_out));
  Button button_7 (.out(button_7_out));
  _7_Segment_Display u_7_segment_display_5 (
    .g(upperdisplay_1_out_27), .f(upperdisplay_1_out_16), .a(upperdisplay_1_out_28),
    .b(upperdisplay_1_out_17), .e(lowerdisplay_1_out_14), .d(lowerdisplay_1_out_15), .c(lowerdisplay_1_out_16));  // open: dp
  _7_Segment_Display u_7_segment_display_6 (
    .g(upperdisplay_1_out_29), .f(upperdisplay_1_out_18), .a(upperdisplay_1_out_30),
    .b(upperdisplay_1_out_19), .e(lowerdisplay_1_out_17), .d(lowerdisplay_1_out_18), .c(lowerdisplay_1_out_19));  // open: dp
  DotMatrix #(.matrixcols(1), .matrixrows(6)) dotmatrix_2 (.col0(lowerdisplay_1_out_13));
  Button button_8 (.out(button_8_out));
  Button button_9 (.out(button_9_out));
  DotMatrix #(.matrixcols(7), .matrixrows(6)) dotmatrix_3 (
    .col0(lowerdisplay_1_out_20), .col1(lowerdisplay_1_out_21), .col2(lowerdisplay_1_out_22),
    .col3(lowerdisplay_1_out_23), .col4(lowerdisplay_1_out_24), .col5(lowerdisplay_1_out_25),
    .col6(lowerdisplay_1_out_26));
  GantiHari DAY (
    .Set(button_2_out), .Reset(button_3_out), .Senin(DAY_senin), .Selasa(DAY_selasa), .Rabu(DAY_rabu),
    .Kamis(DAY_kamis), .Jumat(DAY_jumat), .Sabtu(DAY_sabtu), .Minggu(DAY_minggu));
  LED led_1 (.in(upperdisplay_1_out_8));
  UpperDisplay upperdisplay_1 (
    .out_9(upperdisplay_1_out_9), .out_21(upperdisplay_1_out_21), .out_10(upperdisplay_1_out_10),
    .out_22(upperdisplay_1_out_22), .out_11(upperdisplay_1_out_11), .out_23(upperdisplay_1_out_23),
    .out_12(upperdisplay_1_out_12), .out_24(upperdisplay_1_out_24), .out_13(upperdisplay_1_out_13),
    .out_25(upperdisplay_1_out_25), .out_14(upperdisplay_1_out_14), .out_26(upperdisplay_1_out_26),
    .out_15(upperdisplay_1_out_15), .out_27(upperdisplay_1_out_27), .out_16(upperdisplay_1_out_16),
    .out_28(upperdisplay_1_out_28), .out_17(upperdisplay_1_out_17), .out_29(upperdisplay_1_out_29),
    .out_18(upperdisplay_1_out_18), .out_30(upperdisplay_1_out_30), .out_19(upperdisplay_1_out_19),
    .out_20(upperdisplay_1_out_20), .out_8(upperdisplay_1_out_8), .in_1(button_1_out), .in_2(button_4_out),
    .in_3(button_5_out), .in_4(button_6_out), .in_5(button_7_out), .in_6(button_8_out), .in_7(button_9_out));
  LowerDisplay lowerdisplay_1 (
    .out_24(lowerdisplay_1_out_24), .out_4(lowerdisplay_1_out_4), .out_25(lowerdisplay_1_out_25),
    .out_26(lowerdisplay_1_out_26), .out_5(lowerdisplay_1_out_5), .out_6(lowerdisplay_1_out_6),
    .out_7(lowerdisplay_1_out_7), .out_8(lowerdisplay_1_out_8), .out_9(lowerdisplay_1_out_9),
    .out_10(lowerdisplay_1_out_10), .out_11(lowerdisplay_1_out_11), .out_12(lowerdisplay_1_out_12),
    .out_13(lowerdisplay_1_out_13), .out_2(lowerdisplay_1_out_2), .out_14(lowerdisplay_1_out_14),
    .out_15(lowerdisplay_1_out_15), .out_16(lowerdisplay_1_out_16), .out_17(lowerdisplay_1_out_17),
    .out_18(lowerdisplay_1_out_18), .out_19(lowerdisplay_1_out_19), .out_20(lowerdisplay_1_out_20),
    .out_3(lowerdisplay_1_out_3), .out_21(lowerdisplay_1_out_21), .out_22(lowerdisplay_1_out_22),
    .out_23(lowerdisplay_1_out_23), .in_1(upperdisplay_1_out_20));
  LED Senin (.in(DAY_senin));
  LED Selasa (.in(DAY_selasa));
  LED Rabu (.in(DAY_rabu));
  LED Kamis (.in(DAY_kamis));
  LED Jumat (.in(DAY_jumat));
  LED Sabtu (.in(DAY_sabtu));
  LED Minggu (.in(DAY_minggu));

  // Notes on the sheet:
  //   Day Set
  //   Reset
  //   Hour
  //   minute
  //   Minute
  //   second
  //   Second
  //   Set
  //   AM/PM
  //   Dibuat oleh Kelompok PKA - 07
endmodule

module Decodr (
  input  in_1,
  input  [3:0] in_2,
  output [2:0] out_3,
  output [3:0] out_4
);

  wire and_1_out, and_2_out, and_3_out, and_4_out, and_5_out, and_6_out, and_7_out, and_8_out, and_9_out,
       and_10_out, and_11_out, and_12_out, and_13_out, and_14_out, and_15_out, and_16_out, and_17_out,
       and_18_out, not_1_out, not_2_out, not_3_out, xor_1_out, xor_2_out, xor_3_out;

  or c (out_3[0], in_2[0], xor_2_out, in_2[2]);
  or d (out_3[1], and_1_out, and_2_out, and_3_out, and_4_out);
  and and_1 (and_1_out, xor_1_out, xor_3_out);
  and and_2 (and_2_out, in_2[2], xor_2_out, in_2[0]);
  xor xor_1 (xor_1_out, not_1_out, and_7_out);
  not not_1 (not_1_out, in_2[2]);
  and and_3 (and_3_out, xor_1_out, in_2[1]);
  and and_4 (and_4_out, in_2[1], xor_3_out);
  xor xor_2 (xor_2_out, not_2_out, and_7_out);
  xor xor_3 (xor_3_out, not_3_out, and_7_out);
  not not_2 (not_2_out, in_2[1]);
  not not_3 (not_3_out, in_2[0]);
  or e (out_3[2], and_5_out, and_6_out);
  and and_5 (and_5_out, xor_1_out, xor_3_out);
  and and_6 (and_6_out, in_2[1], xor_3_out);
  and and_7 (and_7_out, ~in_2[3], ~in_2[2], ~in_2[1], ~in_2[0], in_1);  // AND_Gate
  or b (out_4[0], and_8_out, xor_1_out, and_9_out);
  and and_8 (and_8_out, xor_2_out, xor_3_out);
  and and_9 (and_9_out, in_2[1], in_2[0]);
  or a (out_4[1], and_10_out, in_2[3], and_11_out, and_12_out);
  and and_10 (and_10_out, xor_1_out, xor_3_out);
  and and_11 (and_11_out, in_2[2], in_2[0]);
  and and_12 (and_12_out, in_2[1], in_2[0]);
  and and_13 (and_13_out, in_2[2], xor_2_out);
  or f (out_4[2], and_13_out, in_2[3], and_14_out, and_15_out);
  and and_14 (and_14_out, xor_2_out, xor_3_out);
  and and_15 (and_15_out, in_2[2], in_2[1], xor_3_out);
  or g (out_4[3], and_16_out, in_2[3], and_17_out, and_18_out);
  and and_16 (and_16_out, in_2[2], xor_2_out);
  and and_17 (and_17_out, xor_1_out, in_2[1]);
  and and_18 (and_18_out, in_2[1], xor_3_out);
endmodule

module UpperDisplay (
  input  in_1,
  input  in_2,
  input  in_3,
  input  in_4,
  input  in_5,
  input  in_6,
  input  in_7,
  output out_8,
  output out_9,
  output out_10,
  output out_11,
  output out_12,
  output out_13,
  output out_14,
  output out_15,
  output out_16,
  output out_17,
  output out_18,
  output out_19,
  output [16:0] out_20,
  output out_21,
  output out_22,
  output out_23,
  output out_24,
  output out_25,
  output out_26,
  output out_27,
  output out_28,
  output out_29,
  output out_30
);

  wire clock_1_out, counter60jk_1_out_5, counter60jk_1_out_6, counter60jk_2_out_5, counter60jk_2_out_6,
       d_ff_1_qn;
  wire [3:0] counter12_1_out_7, counter60jk_1_out_7, counter60jk_1_out_8, counter60jk_2_out_7,
       counter60jk_2_out_8;

  Counter12 counter12_1 (
    .in_1(in_1), .in_2(in_6), .out_5(out_20[16]), .out_6(out_9), .out_7(counter12_1_out_7),
    .in_3(counter60jk_1_out_5), .in_4(counter60jk_1_out_6));
  Decodr decodr_1 (
    .in_2(counter12_1_out_7), .out_3(out_20[2:0]), .out_4({out_21, out_10, out_22, out_11}));  // open: in_1
  Decodr decodr_2 (
    .in_2(counter60jk_1_out_8), .out_3(out_20[5:3]), .out_4({out_23, out_12, out_24, out_13}));  // open: in_1
  Decodr decodr_3 (
    .in_2(counter60jk_1_out_7), .out_3(out_20[8:6]), .out_4({out_25, out_14, out_26, out_15}));  // open: in_1
  Counter60JK counter60jk_1 (
    .out_5(counter60jk_1_out_5), .out_6(counter60jk_1_out_6), .in_1(in_2), .in_2(in_3),
    .out_8(counter60jk_1_out_8), .out_7(counter60jk_1_out_7), .in_3(counter60jk_2_out_5),
    .in_4(counter60jk_2_out_6));
  Decodr decodr_4 (
    .in_2(counter60jk_2_out_8), .out_3(out_20[11:9]), .out_4({out_27, out_16, out_28, out_17}));  // open: in_1
  Clock clock_1 (.out(clock_1_out));
  Counter60JK counter60jk_2 (
    .out_5(counter60jk_2_out_5), .out_6(counter60jk_2_out_6), .in_1(in_4), .in_2(in_5),
    .out_8(counter60jk_2_out_8), .out_7(counter60jk_2_out_7), .in_3(clock_1_out), .in_4(out_8));
  Decodr decodr_5 (
    .in_2(counter60jk_2_out_7), .out_3(out_20[14:12]), .out_4({out_29, out_18, out_30, out_19}));  // open: in_1
  D_Flip_Flop d_ff_1 (.clk(in_7), .D(d_ff_1_qn), .Q(out_8), .Qn(d_ff_1_qn));  // open: preset, reset

  assign out_20[15] = out_9;
endmodule

module Counter60JK (
  input  in_1,
  input  in_2,
  input  in_3,
  input  in_4,
  output out_5,
  output out_6,
  output [3:0] out_7,
  output [3:0] out_8
);

  wire and_2_out, j_k_ff_1_qn, j_k_ff_2_qn, j_k_ff_4_qn, j_k_ff_5_qn, j_k_ff_6_qn, multiplexer_1_out,
       multiplexer_2_out;

  Multiplexer multiplexer_1 (.in0(and_2_out), .in1(in_1), .out(multiplexer_1_out), .sel(in_4));
  J_K_Flip_Flop j_k_ff_1 (
    .J(1'b1), .K(1'b1), .clk(multiplexer_1_out), .Q(out_8[0]), .Qn(j_k_ff_1_qn), .reset(out_5));  // open: preset
  J_K_Flip_Flop j_k_ff_2 (
    .J(1'b1), .K(1'b1), .clk(j_k_ff_1_qn), .Q(out_8[1]), .Qn(j_k_ff_2_qn), .reset(out_5));  // open: preset
  and and_1 (out_5, out_8[1], out_8[2]);
  J_K_Flip_Flop j_k_ff_3 (.J(1'b1), .K(1'b1), .clk(j_k_ff_2_qn), .Q(out_8[2]), .reset(out_5));  // open: Qn, preset
  J_K_Flip_Flop j_k_ff_4 (
    .J(1'b1), .K(1'b1), .clk(multiplexer_2_out), .Q(out_7[0]), .Qn(j_k_ff_4_qn), .reset(and_2_out));  // open: preset
  Multiplexer multiplexer_2 (.in0(in_3), .in1(in_2), .out(multiplexer_2_out), .sel(in_4));
  J_K_Flip_Flop j_k_ff_5 (
    .J(1'b1), .K(1'b1), .clk(j_k_ff_4_qn), .Q(out_7[1]), .Qn(j_k_ff_5_qn), .reset(and_2_out));  // open: preset
  and and_2 (and_2_out, out_7[1], out_7[3]);
  J_K_Flip_Flop j_k_ff_6 (
    .J(1'b1), .K(1'b1), .clk(j_k_ff_5_qn), .Q(out_7[2]), .Qn(j_k_ff_6_qn), .reset(and_2_out));  // open: preset
  J_K_Flip_Flop j_k_ff_7 (.J(1'b1), .K(1'b1), .clk(j_k_ff_6_qn), .Q(out_7[3]), .reset(and_2_out));  // open: Qn, preset

  assign out_6 = in_4;
  assign out_8[3] = 1'b0;
endmodule

module Counter12 (
  input  in_1,
  input  in_2,
  input  in_3,
  input  in_4,
  output out_5,
  output out_6,
  output [3:0] out_7
);

  wire and_1_out, and_2_out, and_3_out, and_4_out, d_ff_1_qn, j_k_ff_1_qn, j_k_ff_2_qn, j_k_ff_3_qn,
       multiplexer_1_out, multiplexer_2_out, not_1_out, not_2_out;
  wire [3:0] adder_1_out, j_k_ff_1_q, subtractor_1_out;

  Multiplexer #(.disabled("Z")) multiplexer_1 (.in0(and_4_out), .in1(in_1), .out(multiplexer_1_out), .sel(in_4));
  J_K_Flip_Flop j_k_ff_1 (
    .J(1'b1), .K(1'b1), .clk(multiplexer_1_out), .Q(j_k_ff_1_q[0]), .Qn(j_k_ff_1_qn), .reset(and_2_out));  // open: preset
  J_K_Flip_Flop j_k_ff_2 (
    .J(1'b1), .K(1'b1), .clk(j_k_ff_1_qn), .Q(j_k_ff_1_q[1]), .Qn(j_k_ff_2_qn), .reset(and_2_out));  // open: preset
  J_K_Flip_Flop j_k_ff_3 (
    .J(1'b1), .K(1'b1), .clk(j_k_ff_2_qn), .Q(j_k_ff_1_q[2]), .Qn(j_k_ff_3_qn), .reset(and_2_out));  // open: preset
  J_K_Flip_Flop j_k_ff_4 (
    .J(1'b1), .K(1'b1), .clk(j_k_ff_3_qn), .Q(j_k_ff_1_q[3]), .reset(and_2_out));  // open: Qn, preset
  not not_1 (not_1_out, and_1_out);
  and and_1 (and_1_out, j_k_ff_1_q[1], j_k_ff_1_q[0], j_k_ff_1_q[3]);
  and and_2 (and_2_out, j_k_ff_1_q[2], j_k_ff_1_q[3]);
  and and_3 (and_3_out, not_1_out, and_1_out);
  and and_4 (and_4_out, not_2_out, in_3);
  Comparator #(.mode("unsigned"), .width(4)) comparator_1 (.a(adder_1_out), .b(4'b1001), .gt(out_6));  // open: eq, lt
  Multiplexer #(.disabled("Z")) multiplexer_2 (.in0(and_3_out), .in1(in_2), .out(multiplexer_2_out), .sel(in_4));
  not not_2 (not_2_out, in_3);
  Adder #(.width(4)) adder_1 (.a(j_k_ff_1_q), .b(4'b0001), .out(adder_1_out));  // open: cin, cout
  Multiplexer #(.disabled("Z"), .width(4)) multiplexer_3 (
    .in0(adder_1_out), .in1(subtractor_1_out), .out(out_7), .sel(out_6));
  D_Flip_Flop d_ff_1 (.D(d_ff_1_qn), .clk(multiplexer_2_out), .Q(out_5), .Qn(d_ff_1_qn));  // open: preset, reset
  Subtractor #(.width(4)) subtractor_1 (.a(adder_1_out), .b(4'b1010), .out(subtractor_1_out));  // open: bin, bout
endmodule

module LowerDisplay (
  input  [16:0] in_1,
  output out_2,
  output out_3,
  output out_4,
  output out_5,
  output [5:0] out_6,
  output out_7,
  output out_8,
  output out_9,
  output out_10,
  output out_11,
  output out_12,
  output [5:0] out_13,
  output out_14,
  output out_15,
  output out_16,
  output out_17,
  output out_18,
  output out_19,
  output [5:0] out_20,
  output [5:0] out_21,
  output [5:0] out_22,
  output [5:0] out_23,
  output [5:0] out_24,
  output [5:0] out_25,
  output [5:0] out_26
);

  not not_1 (out_22[2], in_1[16]);

  assign out_2 = in_1[15];
  assign out_3 = in_1[2];
  assign out_4 = in_1[1];
  assign out_5 = in_1[0];
  assign out_6 = 6'b010010;
  assign out_7 = in_1[5];
  assign out_8 = in_1[4];
  assign out_9 = in_1[3];
  assign out_10 = in_1[8];
  assign out_11 = in_1[7];
  assign out_12 = in_1[6];
  assign out_13 = 6'b010010;
  assign out_14 = in_1[11];
  assign out_15 = in_1[10];
  assign out_16 = in_1[9];
  assign out_17 = in_1[14];
  assign out_18 = in_1[13];
  assign out_19 = in_1[12];
  assign out_20 = {1'b0, in_1[16], 4'b1110};
  assign out_21 = 6'b010100;
  assign {out_22[5:3], out_22[1:0]} = {3'b001, out_22[2], 1'b0};
  assign out_23 = {6{1'b0}};
  assign out_24 = 6'b011110;
  assign out_25 = 6'b001000;
  assign out_26 = 6'b011110;

  // Notes on the sheet:
  //   out_20: pull=up
endmodule

module WeekdayCounter (
  input  CLOCK,
  input  CLEAR,
  output out_3,
  output out_4,
  output out_5,
  output out_6
);

  wire and_1_out, and_2_out, and_3_out, j_k_ff_2_qn, j_k_ff_3_qn, not_1_out, not_2_out, not_3_out, or_1_out,
       or_2_out;

  or or_1 (or_1_out, j_k_ff_2_qn, j_k_ff_3_qn);
  J_K_Flip_Flop j_k_ff_1 (.J(or_1_out), .K(1'b1), .clk(CLOCK), .Q(out_3), .reset(CLEAR));  // open: Qn, preset
  not not_1 (not_1_out, out_3);
  and and_1 (and_1_out, 1'b1, not_1_out);
  or or_2 (or_2_out, out_3, out_5);
  J_K_Flip_Flop j_k_ff_2 (
    .J(out_3), .K(or_2_out), .clk(CLOCK), .Q(out_4), .Qn(j_k_ff_2_qn), .reset(CLEAR));  // open: preset
  not not_2 (not_2_out, out_4);
  and and_2 (and_2_out, and_1_out, not_2_out);
  and and_3 (and_3_out, out_3, out_4);
  J_K_Flip_Flop j_k_ff_3 (
    .J(and_3_out), .K(out_4), .clk(CLOCK), .Q(out_5), .Qn(j_k_ff_3_qn), .reset(CLEAR));  // open: preset
  not not_3 (not_3_out, out_5);
  and and_4 (out_6, and_2_out, not_3_out);
endmodule

module Encoder (
  input  in_1,
  input  in_2,
  input  in_3,
  output out_4,
  output out_5,
  output out_6,
  output out_7,
  output out_8,
  output out_9,
  output out_10,
  output out_11
);

  wire not_1_out, not_2_out, not_3_out;

  not not_1 (not_1_out, in_1);
  not not_2 (not_2_out, in_2);
  not not_3 (not_3_out, in_3);
  and and_1 (out_4, not_1_out, not_2_out, not_3_out);
  and and_2 (out_5, not_1_out, not_2_out, in_3);
  and and_3 (out_6, not_1_out, in_2, not_3_out);
  and and_4 (out_7, not_1_out, in_2, in_3);
  and and_5 (out_8, in_1, not_2_out, not_3_out);
  and and_6 (out_9, in_1, not_2_out, in_3);
  and and_7 (out_10, in_1, in_2, not_3_out);
  and and_8 (out_11, in_1, in_2, in_3);
endmodule

module GantiHari (
  input  Set,
  input  Reset,
  output Senin,
  output Selasa,
  output Rabu,
  output Kamis,
  output Jumat,
  output Sabtu,
  output Minggu
);

  wire encoder_1_out_11, weekdaycounter_1_out_3, weekdaycounter_1_out_4, weekdaycounter_1_out_5;

  WeekdayCounter weekdaycounter_1 (
    .CLOCK(Set), .CLEAR(Reset), .out_3(weekdaycounter_1_out_3), .out_4(weekdaycounter_1_out_4),
    .out_5(weekdaycounter_1_out_5));  // open: out_6
  Encoder encoder_1 (
    .in_1(weekdaycounter_1_out_5), .in_2(weekdaycounter_1_out_4), .in_3(weekdaycounter_1_out_3),
    .out_4(Senin), .out_5(Selasa), .out_6(Rabu), .out_7(Kamis), .out_8(Jumat), .out_9(Sabtu),
    .out_10(Minggu), .out_11(encoder_1_out_11));
endmodule
